// Logisim project Processor.circ as structural Verilog: 20 circuits, main circuit main
module main (
  input  [3:0] Register_Number,
  input  Reset,
  output [23:0] out_3,
  output [31:0] out_4,
  output [31:0] out_5,
  output [3:0] out_6,
  output [23:0] out_7,
  output [31:0] out_8,
  output [31:0] out_9,
  output [31:0] out_10,
  output [12:0] out_11
);

  wire and_1_out, and_2_out, CLK, DataLockSig, isBeq_OFEX, isBgt_OFEX, isBranchTaken, isCall_MARW,
       isLoad_EXMA, isLoad_MARW, isRet_OFEX, isStore_EXMA, isUBranch_OFEX, isWb_MARW, M1controlOF,
       M2controlOF, M3ControlMA, M3ControlRW, M4ControlMA, M4ControlRW, M6ControlMA, not_1_out, not_2_out,
       or_1_out, or_2_out, storeForward;
  wire [1:0] multiplexer_7_out;
  wire [3:0] ALU_Signals_OFEX, aluSignals, of_1_displayout, of_1_displayout_2;
  wire [12:0] Control, ControlEXMA, ControlOFEX, CTRLOFEX;
  wire [23:0] PC, PCEXMA, PCIFOF, PCMARW, PCOFEX;
  wire [31:0] A, AluEXMA, aluMARW, aluResult, AOFEX, B, BOFEX, bT, bTOFEX, CorrInstruction, ex_ma_1_op2out,
       InsEXMA, ldMARW, ldResult, multiplexer_1_out, multiplexer_2_out, multiplexer_3_out, OF__EX_Latch_aout,
       OF__EX_Latch_bout, OF__EX_Latch_op2out, op2, op2EXMA, op2OFEX;
  wire [31:8] of_1_displayout_3;

  Clock Clock (.out(CLK));
  not not_1 (not_1_out, DataLockSig);
  IF if_1 (
    .isBranchTaken(isBranchTaken), .Instruction(out_5), .branchTarget(out_3), .IFstageclock(and_1_out),
    .PC(PC), .reset(Reset));
  and and_1 (and_1_out, CLK, not_2_out);
  not not_2 (not_2_out, DataLockSig);
  MA ma_1 (
    .ldResult(ldResult), .op2(op2EXMA), .isLd(isLoad_EXMA), .isSt(isStore_EXMA), .ALUResult(AluEXMA),
    .Clock(CLK));
  and and_2 (and_2_out, not_1_out, CLK);
  IF_OF if_of_1 (.INSIN(CorrInstruction), .CLKIN(and_2_out), .PCIN(PC), .InsOut(out_8), .PcOut(PCIFOF));
  Multiplexer #(.width(32), .enable("false")) multiplexer_1 (
    .in0(out_8), .in1(32'h68000000), .out(multiplexer_1_out), .sel(or_1_out));
  Multiplexer #(.width(32), .enable("false")) multiplexer_2 (
    .in0(op2), .in1(out_4), .out(multiplexer_2_out), .sel(M2controlOF));
  Multiplexer #(.width(32), .enable("false")) multiplexer_3 (
    .in0(A), .in1(out_4), .out(multiplexer_3_out), .sel(M1controlOF));
  CU cu_1 (
    .isSt(storeForward), .Instruction(out_9));  // open: isWb, isUbranch, isImmediate, isLd, isBeq, isBgt, isCall, isRet, ALUSignals
  OF_EX OF__EX_Latch (
    .InsIN(multiplexer_1_out), .PcIn(PCIFOF), .ControlIn(CTRLOFEX), .BranchTargetIn(bT), .CLKOFEX(CLK),
    .AIn(multiplexer_3_out), .BIn(B), .OP2In(multiplexer_2_out), .InsOut(out_9), .PcOut(PCOFEX),
    .ControlOut(ControlOFEX), .BranchTargetOut(bTOFEX), .AOut(OF__EX_Latch_aout), .BOut(OF__EX_Latch_bout),
    .OP2Out(OF__EX_Latch_op2out));
  MA_RW ma_rw_1 (
    .PCIn(PCEXMA), .LdIn(ldResult), .AluIn(AluEXMA), .CLK(CLK), .InsIn(InsEXMA), .CtrlIn(ControlEXMA),
    .PCOut(PCMARW), .LdOut(ldMARW), .AluOut(aluMARW), .InsOut(out_10), .CtrlOut(out_11));
  OF of_1 (
    .Instruction(out_8), .PC(PCIFOF), .branchTarget(bT), .isSt(Control[12]), .isImmx(Control[2]), .A(A),
    .B(B), .op2(op2), .isRet(Control[9]), .writeData(out_4), .writeAddress(out_6), .isWb(isWb_MARW),
    .clock(CLK), .displayAddress(Register_Number),
    .displayOut({of_1_displayout_3, of_1_displayout_2, of_1_displayout}), .isCall(isCall_MARW));
  EXU exu_1 (
    .isBeq(isBeq_OFEX), .isUbranch(isUBranch_OFEX), .isBgt(isBgt_OFEX), .branchTargetIn(bTOFEX), .A(AOFEX),
    .aluSignals(ALU_Signals_OFEX), .B(BOFEX), .Clock(CLK), .isBranchTaken(isBranchTaken),
    .branchTargetOut(out_3), .ALUResult(aluResult), .isRet(isRet_OFEX));
  Multiplexer #(.width(13), .enable("false")) multiplexer_4 (
    .in0({Control[12:7], aluSignals, Control[2:0]}), .in1({13{1'b0}}), .out(CTRLOFEX), .sel(or_2_out));
  or or_1 (or_1_out, DataLockSig, isBranchTaken);
  Multiplexer #(.select(2), .width(32), .enable("false")) multiplexer_5 (
    .in0(OF__EX_Latch_aout), .in1(out_4), .in2(AluEXMA), .in3(AluEXMA), .out(AOFEX),
    .sel({M3ControlMA, M3ControlRW}));
  Multiplexer #(.select(2), .width(32), .enable("false")) multiplexer_6 (
    .in0(OF__EX_Latch_bout), .in1(out_4), .in2(AluEXMA), .in3(AluEXMA), .out(BOFEX), .sel(multiplexer_7_out));
  Multiplexer #(.width(2), .enable("false")) multiplexer_7 (
    .in0({M4ControlMA, M4ControlRW}), .in1(2'b00), .out(multiplexer_7_out), .sel(storeForward));
  Split_Control split_control_1 (
    .Control_In(ControlOFEX), .isUbranch_out(isUBranch_OFEX), .ALU_signals(ALU_Signals_OFEX),
    .isBeq_out(isBeq_OFEX), .isRet_out(isRet_OFEX), .isBgt_out(isBgt_OFEX));  // open: isWb_out, isImm_out, isLoad_out, isCall_out, isStore_out
  RW rw_1 (
    .Instruction(out_10), .ldResult(ldMARW), .isLd(isLoad_MARW), .ALUResult(aluMARW), .isCall(isCall_MARW),
    .PC(PCMARW), .Address(out_6), .storeData(out_4));
  Hex_Digit_Display hex_digit_display_1 (.value(of_1_displayout_3[31:28]));  // open: dp
  or or_2 (or_2_out, DataLockSig, isBranchTaken);
  Multiplexer #(.width(32), .enable("false")) multiplexer_8 (
    .in0(OF__EX_Latch_op2out), .in1(out_4), .out(op2OFEX), .sel(M4ControlRW));
  Algo5 Algo5DataLock (.A(out_8), .B(out_9), .outbit(DataLockSig));
  Algo7 algo7_1 (.A(InsEXMA), .B(out_10), .Algo7Out(M6ControlMA));
  Hex_Digit_Display hex_digit_display_2 (.value(of_1_displayout_3[23:20]));  // open: dp
  Hex_Digit_Display hex_digit_display_3 (.value(of_1_displayout_3[27:24]));  // open: dp
  Split_Control split_control_2 (
    .Control_In(out_11), .isWb_out(isWb_MARW), .isLoad_out(isLoad_MARW), .isCall_out(isCall_MARW));  // open: isUbranch_out, isImm_out, ALU_signals, isBeq_out, isRet_out, isBgt_out, isStore_out
  Hex_Digit_Display hex_digit_display_4 (.value(of_1_displayout_3[15:12]));  // open: dp
  Hex_Digit_Display hex_digit_display_5 (.value(of_1_displayout_3[19:16]));  // open: dp
  CU cu_2 (
    .isWb(Control[0]), .isUbranch(Control[1]), .isImmediate(Control[2]), .isLd(Control[7]),
    .isSt(Control[12]), .isBeq(Control[8]), .isBgt(Control[11]), .isCall(Control[10]), .isRet(Control[9]),
    .ALUSignals(aluSignals), .Instruction(out_8));
  Hex_Digit_Display hex_digit_display_6 (.value(of_1_displayout_2));  // open: dp
  Hex_Digit_Display hex_digit_display_7 (.value(of_1_displayout_3[11:8]));  // open: dp
  Hex_Digit_Display hex_digit_display_8 (.value(of_1_displayout));  // open: dp
  EX_MA ex_ma_1 (
    .PcIn(PCOFEX), .AluIn(aluResult), .InsIn(out_9), .ClkIN(CLK), .op2In(op2OFEX), .ControlIn(ControlOFEX),
    .PcOut(PCEXMA), .AluOut(AluEXMA), .InsOut(InsEXMA), .Op2Out(ex_ma_1_op2out), .ControlOut(ControlEXMA));
  Multiplexer #(.width(32), .enable("false")) multiplexer_9 (
    .in0(ex_ma_1_op2out), .in1(out_4), .out(op2EXMA), .sel(M6ControlMA));
  Algo7 algo7_2 (.A(out_9), .B(InsEXMA), .Algo7Out(M4ControlMA));
  Split_Control split_control_3 (
    .Control_In(ControlEXMA), .isLoad_out(isLoad_EXMA), .isStore_out(isStore_EXMA));  // open: isWb_out, isUbranch_out, isImm_out, ALU_signals, isBeq_out, isRet_out, isCall_out, isBgt_out
  Algo6 Algo6RWtoOF (.A(out_8), .B(out_10), .Algo6Out(M1controlOF));
  Algo7 Algo7RWOF (.A(out_8), .B(out_10), .Algo7Out(M2controlOF));
  Multiplexer #(.width(32), .enable("false")) multiplexer_10 (
    .in0(out_5), .in1(32'h68000000), .out(CorrInstruction), .sel(isBranchTaken));
  Algo6 algo6_1 (.A(out_9), .B(InsEXMA), .Algo6Out(M3ControlMA));
  Algo6 algo6_2 (.A(out_9), .B(out_10), .Algo6Out(M3ControlRW));
  Algo7 algo7_3 (.A(out_9), .B(out_10), .Algo7Out(M4ControlRW));

  assign out_7 = out_3;

  // Other names for the same wires on the sheet: Address[3:0] = out_6; branchTarget[23:0] = out_3; isWb = Control[0];
  //   isUbranch = Control[1]; isImmediate = Control[2]; Control[6:3] = aluSignals; isLd = Control[7];
  //   isBeq = Control[8]; isRet = Control[9]; isCall = Control[10]; isBgt = Control[11]; isSt = Control[12];
  //   controlMARW[12:0] = out_11; InsIFOF[31:0] = out_8; InsMARW[31:0] = out_10; InsOFEX[31:0] = out_9;
  //   Instruction[31:0] = out_5; storeData[31:0] = out_4

  // Notes on the sheet:
  //   Note: The last instruction should be provided as "ffffffff" otherwise it will keep on interpreting "00000000", i.e. it will keep on doubling r0.
  //   Inserting nop for data lock
endmodule

module IF (
  input  [23:0] branchTarget,
  input  isBranchTaken,
  input  IFstageclock,
  input  reset,
  output [31:0] Instruction,
  output [23:0] PC
);

  wire and_1_out, multiplexer_1_out, not_1_out, not_2_out;

  not not_1 (not_1_out, IFstageclock);
  not not_2 (not_2_out, isBranchTaken);
  Multiplexer #(.enable("false")) multiplexer_1 (.in0(not_1_out), .in1(1'b1), .out(multiplexer_1_out), .sel(and_1_out));
  Counter #(.width(24), .max('hffffff)) counter_1 (
    .load(isBranchTaken), .D(branchTarget), .count(not_2_out), .Q(PC), .clk(multiplexer_1_out), .clr(reset));  // open: carry
  ROM #(.addrWidth(24), .dataWidth(32)) rom_1 (.addr(PC), .data(Instruction));  // open: sel
  and and_1 (and_1_out, Instruction[31], Instruction[30], Instruction[29], Instruction[28], Instruction[27], Instruction[26], Instruction[25], Instruction[24], Instruction[23], Instruction[22], Instruction[21], Instruction[20], Instruction[19], Instruction[18], Instruction[17], Instruction[16], Instruction[14], Instruction[13], Instruction[12], Instruction[11], Instruction[10], Instruction[9], Instruction[8], Instruction[7], Instruction[6], Instruction[5], Instruction[4], Instruction[3], Instruction[2], Instruction[1], Instruction[0], Instruction[15]);

  // Notes on the sheet:
  //   reset: pull=down
  //   IF Stage
  //   Counter for going to the next instruction
  //   Note: The last instruction should be provided as "ffffffff" otherwise it will keep on interpreting "00000000", i.e. it will keep on doubling r0.
  //   contents of rom_1 (hex, n*v repeats v):
  //   4c00000a 98000002 90000000 2c000001 88000003 4c400001 a0000000 fb80008 7c380000 7ff80004 c000001
  //   9ffffff8 77f80004 74380000 7b80008 10404000 a0000000 68000000 68000000 68000000 ffffffff 80000007
  //   4880001 97fffff4 4440001 97ffffed 4000001 97ffffe9 90000000 68000000 68000000 ffffffff
  //   Used to stop instruction processing on encountering code "ffffffff".
endmodule

module OF (
  input  isRet,
  input  [23:0] PC,
  input  isImmx,
  input  [31:0] Instruction,
  input  isCall,
  input  [3:0] writeAddress,
  input  [31:0] writeData,
  input  isWb,
  input  clock,
  input  isSt,
  input  [3:0] displayAddress,
  output [31:0] A,
  output [31:0] op2,
  output [31:0] B,
  output [31:0] displayOut,
  output [31:0] branchTarget
);

  wire and_1_out, or_1_out;
  wire [3:0] multiplexer_2_out, multiplexer_3_out;
  wire [31:0] adder_1_out, bit_extender_1_out, bit_extender_2_out, bit_extender_3_out, bit_extender_4_out,
       immx, shifter_1_out;

  assign bit_extender_1_out = {{5{Instruction[26]}}, Instruction[26:0]};  // Bit_Extender bit_extender_1
  assign bit_extender_2_out = {{8{1'b0}}, PC};  // Bit_Extender bit_extender_2
  Multiplexer #(.width(32), .enable("false")) multiplexer_1 (
    .in0(adder_1_out), .in1(A), .out(branchTarget), .sel(isRet));
  Adder #(.width(32)) adder_1 (.a(bit_extender_1_out), .b(bit_extender_2_out), .out(adder_1_out));  // open: cin, cout
  assign bit_extender_3_out = {{16{Instruction[15]}}, Instruction[15:0]};  // Bit_Extender bit_extender_3
  assign bit_extender_4_out = {{16{1'b0}}, Instruction[15:0]};  // Bit_Extender bit_extender_4
  Shifter #(.width(32)) shifter_1 (.in(bit_extender_4_out), .\dist (5'b10000), .out(shifter_1_out));
  Multiplexer #(.width(4), .enable("false")) multiplexer_2 (
    .in0(Instruction[21:18]), .in1(4'b1111), .out(multiplexer_2_out), .sel(isRet));
  Multiplexer #(.width(4), .enable("false")) multiplexer_3 (
    .in0(Instruction[17:14]), .in1(Instruction[25:22]), .out(multiplexer_3_out), .sel(isSt));
  Multiplexer #(.select(2), .width(32), .enable("false")) multiplexer_4 (
    .in0(bit_extender_3_out), .in1(bit_extender_4_out), .in2(shifter_1_out), .out(immx),
    .sel(Instruction[17:16]));  // open: in3
  regFile regfile_1 (
    .writeData(writeData), .writeAddress(writeAddress), .clock(and_1_out), .readB(multiplexer_3_out),
    .outB(op2), .outA(A), .readA(multiplexer_2_out), .displayOut(displayOut), .displayRead(displayAddress));
  and and_1 (and_1_out, or_1_out, clock);
  or or_1 (or_1_out, isCall, isWb);
  Multiplexer #(.width(32), .enable("false")) multiplexer_5 (.in0(op2), .in1(immx), .out(B), .sel(isImmx));

  // Notes on the sheet:
  //   (Branch Target Calculation)
  //   (27 bit offset)
  //   OF Stage (Edited)
  //   (has Return Address
  //   when instruction is ret)
  //   (Registers from RW Stage moved here to maintain consistency)
  //   rs1
  //   rs2
  //   rd
  //   (modifier bits)
  //   19:22
  //   15:18
  //   23:26
  //   (Immediate Calculation)
  //   (no modifier)
  //   (modifier u)
  //   (modifier h)
  //   (Register Access)
  //   (32 bit modifed immediate)
  //   (OF Outputs)
endmodule

module MA (
  input  [31:0] ALUResult,
  input  isLd,
  input  Clock,
  input  isSt,
  input  [31:0] op2,
  output [31:0] ldResult
);

  wire and_1_out, not_1_out, xor_1_out;
  wire [31:0] shifter_1_out;

  Shifter #(.width(32), .shift("ar")) shifter_1 (.in(ALUResult), .\dist (5'b00010), .out(shifter_1_out));
  and and_1 (and_1_out, isSt, Clock);
  xor xor_1 (xor_1_out, isLd, and_1_out);
  not not_1 (not_1_out, isSt);
  RAM #(.addrWidth(24), .dataWidth(32), .bus("asynch")) ram_1 (
    .addr(shifter_1_out[23:0]), .data(ldResult), .sel(xor_1_out), .ld(not_1_out));  // open: clr
  assign ldResult = isSt ? op2 : 32'bz;  // Controlled_Buffer controlled_buffer_1

  // Notes on the sheet:
  //   MA  Stage
  //   Memory Address
  //   (Data to be stored)
endmodule

module RW (
  input  [31:0] ALUResult,
  input  [31:0] ldResult,
  input  isLd,
  input  [23:0] PC,
  input  isCall,
  input  [31:0] Instruction,
  output [31:0] storeData,
  output [3:0] Address
);

  wire [31:0] adder_1_out, bit_extender_1_out;

  assign bit_extender_1_out = {{8{1'b0}}, PC};  // Bit_Extender bit_extender_1
  Multiplexer #(.width(4), .enable("false")) multiplexer_1 (
    .in0(Instruction[25:22]), .in1(4'b1111), .out(Address), .sel(isCall));
  Adder #(.width(32)) adder_1 (.a(bit_extender_1_out), .b(32'h1), .out(adder_1_out));  // open: cin, cout
  Multiplexer #(.select(2), .width(32), .enable("false")) multiplexer_2 (
    .in0(ALUResult), .in1(ldResult), .in2(adder_1_out), .out(storeData), .sel({isCall, isLd}));  // open: in3

  // Notes on the sheet:
  //   PC: pull=down
  //   storeData: pull=down
  //   Address: pull=down
  //   RW Stage (Edited)
  //   (for arithmetic instructions)
  //   (data loaded from memory)
  //   (to update return address)
  //   (Register to be written to)
  //   (Registers moved to OF Stage to maintain consistency)
  //   (Integer to be written back in register)
endmodule

module regFile (
  input  clock,
  input  [3:0] readA,
  input  [31:0] writeData,
  input  [3:0] readB,
  input  [3:0] writeAddress,
  input  [3:0] displayRead,
  output [31:0] outA,
  output [31:0] outB,
  output [31:0] displayOut
);

  wire counter_1_q;
  wire [31:0] demultiplexer_1_out0, demultiplexer_1_out1, demultiplexer_1_out2, demultiplexer_1_out3,
       demultiplexer_1_out4, demultiplexer_1_out5, demultiplexer_1_out6, demultiplexer_1_out7,
       demultiplexer_1_out8, demultiplexer_1_out9, demultiplexer_1_out10, demultiplexer_1_out11,
       demultiplexer_1_out12, demultiplexer_1_out13, demultiplexer_1_out14, demultiplexer_1_out15,
       multiplexer_1_out, r0, r1, r2, r3, r4, r5, r6, r7, r8, r9, r10, r11, r12, r13, r14, r15;

  Demultiplexer #(.select(4), .width(32), .tristate("true"), .enable("false")) demultiplexer_1 (
    .out0(demultiplexer_1_out0), .out1(demultiplexer_1_out1), .out2(demultiplexer_1_out2),
    .out3(demultiplexer_1_out3), .out4(demultiplexer_1_out4), .out5(demultiplexer_1_out5),
    .out6(demultiplexer_1_out6), .out7(demultiplexer_1_out7), .out8(demultiplexer_1_out8),
    .out9(demultiplexer_1_out9), .out10(demultiplexer_1_out10), .out11(demultiplexer_1_out11),
    .out12(demultiplexer_1_out12), .out13(demultiplexer_1_out13), .out14(demultiplexer_1_out14),
    .out15(demultiplexer_1_out15), .in(writeData), .sel(writeAddress));
  Counter #(.width(1), .max('h1), .ongoal("stay")) counter_1 (
    .Q(counter_1_q), .clk(clock));  // open: load, D, count, carry, clr
  Multiplexer #(.width(32), .enable("false")) multiplexer_1 (
    .in0(32'h3fffffc), .in1(demultiplexer_1_out14), .out(multiplexer_1_out), .sel(counter_1_q));
  Register #(.width(32)) u_r0 (.D(demultiplexer_1_out0), .Q(r0), .clk(clock));  // open: en, clr
  Register #(.width(32)) u_r1 (.D(demultiplexer_1_out1), .Q(r1), .clk(clock));  // open: en, clr
  Register #(.width(32)) u_r2 (.D(demultiplexer_1_out2), .Q(r2), .clk(clock));  // open: en, clr
  Register #(.width(32)) u_r3 (.D(demultiplexer_1_out3), .Q(r3), .clk(clock));  // open: en, clr
  Register #(.width(32)) u_r4 (.D(demultiplexer_1_out4), .Q(r4), .clk(clock));  // open: en, clr
  Register #(.width(32)) u_r5 (.D(demultiplexer_1_out5), .Q(r5), .clk(clock));  // open: en, clr
  Register #(.width(32)) u_r6 (.D(demultiplexer_1_out6), .Q(r6), .clk(clock));  // open: en, clr
  Register #(.width(32)) u_r7 (.D(demultiplexer_1_out7), .Q(r7), .clk(clock));  // open: en, clr
  Register #(.width(32)) u_r8 (.D(demultiplexer_1_out8), .Q(r8), .clk(clock));  // open: en, clr
  Register #(.width(32)) u_r9 (.D(demultiplexer_1_out9), .Q(r9), .clk(clock));  // open: en, clr
  Register #(.width(32)) u_r10 (.D(demultiplexer_1_out10), .Q(r10), .clk(clock));  // open: en, clr
  Register #(.width(32)) u_r11 (.D(demultiplexer_1_out11), .Q(r11), .clk(clock));  // open: en, clr
  Register #(.width(32)) u_r12 (.D(demultiplexer_1_out12), .Q(r12), .clk(clock));  // open: en, clr
  Register #(.width(32)) u_r13 (.D(demultiplexer_1_out13), .Q(r13), .clk(clock));  // open: en, clr
  Register #(.width(32)) u_r14 (.D(multiplexer_1_out), .Q(r14), .clk(clock));  // open: en, clr
  Register #(.width(32)) u_r15 (.D(demultiplexer_1_out15), .Q(r15), .clk(clock));  // open: en, clr
  Multiplexer #(.select(4), .width(32), .disabled(0), .enable("false")) multiplexer_2 (
    .in0(r0), .in1(r1), .in2(r2), .in3(r3), .in4(r4), .in5(r5), .in6(r6), .in7(r7), .in8(r8), .in9(r9),
    .in10(r10), .in11(r11), .in12(r12), .in13(r13), .in14(r14), .in15(r15), .out(outA), .sel(readA));
  Multiplexer #(.select(4), .width(32), .disabled(0), .enable("false")) multiplexer_3 (
    .in0(r0), .in1(r1), .in2(r2), .in3(r3), .in4(r4), .in5(r5), .in6(r6), .in7(r7), .in8(r8), .in9(r9),
    .in10(r10), .in11(r11), .in12(r12), .in13(r13), .in14(r14), .in15(r15), .out(outB), .sel(readB));
  Multiplexer #(.select(4), .width(32), .disabled(0), .enable("false")) multiplexer_4 (
    .in0(r0), .in1(r1), .in2(r2), .in3(r3), .in4(r4), .in5(r5), .in6(r6), .in7(r7), .in8(r8), .in9(r9),
    .in10(r10), .in11(r11), .in12(r12), .in13(r13), .in14(r14), .in15(r15), .out(displayOut),
    .sel(displayRead));

  // Notes on the sheet:
  //   outB: pull=down
  //   displayOut: pull=down
  //   writeAddress: pull=down
  //   displayRead: pull=down
  //   readB: pull=down
  //   outA: pull=down
  //   writeData: pull=down
  //   readA: pull=down
  //   (for RW Stage)
  //   (to initialize stack pointer
  //   to last memory location)
  //   (to fetch Operand 1)
  //   (to fetch Operand 2)
  //   (for external display)
endmodule

module CU (
  input  [31:0] Instruction,
  output isWb,
  output isUbranch,
  output isImmediate,
  output isLd,
  output isSt,
  output isBeq,
  output isBgt,
  output isCall,
  output isRet,
  output [3:0] ALUSignals
);

  wire and_1_out, and_2_out, and_3_out, and_4_out, demultiplexer_1_out0, demultiplexer_1_out1, isAdd, isAnd,
       isAsr, isCmp, isDiv, isLsl, isLsr, isMod, isMov, isMul, isNot, isOr, not_1_out, not_2_out, not_3_out,
       not_4_out, not_5_out, not_6_out, not_7_out, or_1_out, or_2_out;
  wire [3:0] adder_1_out, adder_2_out, adder_3_out, adder_4_out, adder_5_out, adder_6_out, adder_7_out,
       adder_8_out, adder_9_out, adder_10_out, adder_11_out, bit_extender_1_out, bit_extender_2_out,
       bit_extender_3_out, bit_extender_4_out, bit_extender_5_out, bit_extender_6_out, bit_extender_7_out,
       bit_extender_8_out, bit_extender_9_out, bit_extender_10_out, bit_extender_11_out, bit_extender_12_out,
       bit_extender_13_out, multiplier_1_out, multiplier_2_out, multiplier_3_out, multiplier_4_out,
       multiplier_5_out, multiplier_6_out, multiplier_7_out, multiplier_8_out, multiplier_9_out,
       multiplier_10_out, multiplier_11_out, multiplier_12_out;

  not not_1 (not_1_out, Instruction[28]);
  not not_2 (not_2_out, Instruction[29]);
  not not_3 (not_3_out, Instruction[28]);
  not not_4 (not_4_out, Instruction[27]);
  not not_5 (not_5_out, Instruction[31]);
  Demultiplexer #(.select(5), .disabled(0), .enable("false")) demultiplexer_1 (
    .out0(demultiplexer_1_out0), .out1(demultiplexer_1_out1), .out2(isMul), .out3(isDiv), .out4(isMod),
    .out5(isCmp), .out6(isAnd), .out7(isOr), .out8(isNot), .out9(isMov), .out10(isLsl), .out11(isLsr),
    .out12(isAsr), .out14(isLd), .out15(isSt), .out16(isBeq), .out17(isBgt), .out19(isCall), .out20(isRet),
    .in(1'b1), .sel(Instruction[31:27]));  // open: out13, out18, out21, out22, out23, out24, out25, out26, out27, out28, out29, out30, out31
  not not_6 (not_6_out, Instruction[31]);
  or or_1 (or_1_out, Instruction[30], not_1_out);
  and and_1 (and_1_out, not_2_out, Instruction[28]);
  and and_2 (and_2_out, Instruction[29], not_3_out, not_4_out);
  and and_3 (and_3_out, Instruction[28], Instruction[29], Instruction[30], not_5_out);
  and and_4 (and_4_out, not_6_out, Instruction[29], Instruction[27], or_1_out);
  not not_7 (not_7_out, Instruction[30]);
  or or_2 (or_2_out, and_1_out, and_2_out);
  nor nor_1 (isWb, Instruction[31], and_4_out);
  and and_5 (isUbranch, Instruction[31], not_7_out, or_2_out);
  or or_3 (isAdd, and_3_out, demultiplexer_1_out0);
  assign bit_extender_1_out = {{3{1'b0}}, demultiplexer_1_out1};  // Bit_Extender bit_extender_1
  assign bit_extender_2_out = {{3{1'b0}}, isCmp};  // Bit_Extender bit_extender_2
  assign bit_extender_3_out = {{3{1'b0}}, isMul};  // Bit_Extender bit_extender_3
  assign bit_extender_4_out = {{3{1'b0}}, isDiv};  // Bit_Extender bit_extender_4
  assign bit_extender_5_out = {{3{1'b0}}, isMod};  // Bit_Extender bit_extender_5
  assign bit_extender_6_out = {{3{1'b0}}, isLsl};  // Bit_Extender bit_extender_6
  assign bit_extender_7_out = {{3{1'b0}}, isLsr};  // Bit_Extender bit_extender_7
  assign bit_extender_8_out = {{3{1'b0}}, isAsr};  // Bit_Extender bit_extender_8
  assign bit_extender_9_out = {{3{1'b0}}, isOr};  // Bit_Extender bit_extender_9
  assign bit_extender_10_out = {{3{1'b0}}, isNot};  // Bit_Extender bit_extender_10
  assign bit_extender_11_out = {{3{1'b0}}, isAnd};  // Bit_Extender bit_extender_11
  assign bit_extender_12_out = {{3{1'b0}}, isMov};  // Bit_Extender bit_extender_12
  assign bit_extender_13_out = {{3{1'b0}}, isAdd};  // Bit_Extender bit_extender_13
  Multiplier #(.width(4)) multiplier_1 (
    .a(bit_extender_1_out), .b(4'b0010), .out(multiplier_1_out));  // open: cin, cout
  Multiplier #(.width(4)) multiplier_2 (
    .a(bit_extender_2_out), .b(4'b0011), .out(multiplier_2_out));  // open: cin, cout
  Multiplier #(.width(4)) multiplier_3 (
    .a(bit_extender_3_out), .b(4'b0100), .out(multiplier_3_out));  // open: cin, cout
  Multiplier #(.width(4)) multiplier_4 (
    .a(bit_extender_4_out), .b(4'b0101), .out(multiplier_4_out));  // open: cin, cout
  Multiplier #(.width(4)) multiplier_5 (
    .a(bit_extender_5_out), .b(4'b0110), .out(multiplier_5_out));  // open: cin, cout
  Multiplier #(.width(4)) multiplier_6 (
    .a(bit_extender_6_out), .b(4'b0111), .out(multiplier_6_out));  // open: cin, cout
  Multiplier #(.width(4)) multiplier_7 (
    .a(bit_extender_7_out), .b(4'b1000), .out(multiplier_7_out));  // open: cin, cout
  Multiplier #(.width(4)) multiplier_8 (
    .a(bit_extender_8_out), .b(4'b1001), .out(multiplier_8_out));  // open: cin, cout
  Multiplier #(.width(4)) multiplier_9 (
    .a(bit_extender_9_out), .b(4'b1010), .out(multiplier_9_out));  // open: cin, cout
  Multiplier #(.width(4)) multiplier_10 (
    .a(bit_extender_10_out), .b(4'b1011), .out(multiplier_10_out));  // open: cin, cout
  Multiplier #(.width(4)) multiplier_11 (
    .a(bit_extender_11_out), .b(4'b1100), .out(multiplier_11_out));  // open: cin, cout
  Multiplier #(.width(4)) multiplier_12 (
    .a(bit_extender_12_out), .b(4'b1101), .out(multiplier_12_out));  // open: cin, cout
  Adder #(.width(4)) adder_1 (.a(bit_extender_13_out), .b(multiplier_1_out), .out(adder_1_out));  // open: cin, cout
  Adder #(.width(4)) adder_2 (.a(multiplier_2_out), .b(multiplier_3_out), .out(adder_2_out));  // open: cin, cout
  Adder #(.width(4)) adder_3 (.a(multiplier_4_out), .b(multiplier_5_out), .out(adder_3_out));  // open: cin, cout
  Adder #(.width(4)) adder_4 (.a(multiplier_6_out), .b(multiplier_7_out), .out(adder_4_out));  // open: cin, cout
  Adder #(.width(4)) adder_5 (.a(multiplier_8_out), .b(multiplier_9_out), .out(adder_5_out));  // open: cin, cout
  Adder #(.width(4)) adder_6 (.a(multiplier_10_out), .b(multiplier_11_out), .out(adder_6_out));  // open: cin, cout
  Adder #(.width(4)) adder_7 (.a(adder_1_out), .b(adder_2_out), .out(adder_7_out));  // open: cin, cout
  Adder #(.width(4)) adder_8 (.a(adder_3_out), .b(adder_4_out), .out(adder_8_out));  // open: cin, cout
  Adder #(.width(4)) adder_9 (.a(adder_5_out), .b(adder_6_out), .out(adder_9_out));  // open: cin, cout
  Adder #(.width(4)) adder_10 (.a(adder_7_out), .b(adder_8_out), .out(adder_10_out));  // open: cin, cout
  Adder #(.width(4)) adder_11 (.a(adder_9_out), .b(multiplier_12_out), .out(adder_11_out));  // open: cin, cout
  Adder #(.width(4)) adder_12 (.a(adder_10_out), .b(adder_11_out), .out(ALUSignals));  // open: cin, cout

  assign isImmediate = Instruction[26];

  // Notes on the sheet:
  //   Instruction: pull=down
  //   opcode
  //   (Circuit for signals created by multiple instructions)
  //   (Demultiplexer for Control Signals created by single instructions)
  //   Create ALUSignals
endmodule

module ALU (
  input  [31:0] A,
  input  [3:0] aluSignals,
  input  [31:0] B,
  input  clock,
  output [31:0] aluResult,
  output flags_GT,
  output flags_E
);

  wire [31:0] Add, addA, addB, And, andA, andB, Asr, asrA, asrB, cmpA, cmpB, Div, divA, divB, Lsl, lslA,
       lslB, Lsr, lsrA, lsrB, Mod, modA, modB, movB, Mul, mulA, mulB, Not, notB, Or, orA, orB, register_1_q,
       register_2_q, Sub, subA, subB;

  Demultiplexer #(.select(4), .width(32), .tristate("true"), .enable("false")) demultiplexer_1 (
    .out1(addA), .out2(subA), .out3(cmpA), .out4(mulA), .out5(divA), .out6(modA), .out7(lslA), .out8(lsrA),
    .out9(asrA), .out10(orA), .out12(andA), .in(A), .sel(aluSignals));  // open: out0, out11, out13, out14, out15
  Demultiplexer #(.select(4), .width(32), .tristate("true"), .disabled(0), .enable("false")) demultiplexer_2 (
    .out1(addB), .out2(subB), .out3(cmpB), .out4(mulB), .out5(divB), .out6(modB), .out7(lslB), .out8(lsrB),
    .out9(asrB), .out10(orB), .out11(notB), .out12(andB), .out13(movB), .in(B), .sel(aluSignals));  // open: out0, out14, out15
  Adder #(.width(32)) adder_1 (.a(addA), .b(addB), .out(Add));  // open: cin, cout
  Subtractor #(.width(32)) subtractor_1 (.a(subA), .b(subB), .out(Sub));  // open: bin, bout
  Shifter #(.width(32)) shifter_1 (.in(lslA), .\dist (lslB[4:0]), .out(Lsl));
  Shifter #(.width(32), .shift("lr")) shifter_2 (.in(lsrA), .\dist (lsrB[4:0]), .out(Lsr));
  Shifter #(.width(32), .shift("ar")) shifter_3 (.in(asrA), .\dist (asrB[4:0]), .out(Asr));
  Register #(.width(32)) register_1 (.D(cmpA), .Q(register_1_q), .clk(clock));  // open: en, clr
  Register #(.width(32)) register_2 (.D(cmpB), .Q(register_2_q), .clk(clock));  // open: en, clr
  Comparator #(.width(32)) comparator_1 (.a(register_1_q), .b(register_2_q), .gt(flags_GT), .eq(flags_E));  // open: lt
  Multiplier #(.width(32)) multiplier_1 (.a(mulA), .b(mulB), .out(Mul));  // open: cin, cout
  Divider #(.width(32)) divider_1 (.a(divA), .b(divB), .out(Div));  // open: upper, rem
  Divider #(.width(32)) divider_2 (.a(modA), .b(modB), .rem(Mod));  // open: out, upper
  Multiplexer #(.select(4), .width(32), .disabled(0)) multiplexer_1 (
    .in1(Add), .in2(Sub), .in4(Mul), .in5(Div), .in6(Mod), .in7(Lsl), .in8(Lsr), .in9(Asr), .in10(Or),
    .in11(Not), .in12(And), .in13(movB), .out(aluResult), .sel(aluSignals), .en(1'b1));  // open: in0, in3, in14, in15
  assign Or = orA | orB;  // OR_Gate or_1, 32 bits wide
  assign And = andA & andB;  // AND_Gate and_1, 32 bits wide
  assign Not = ~notB;  // NOT_Gate not_1, 32 bits wide

  // Notes on the sheet:
  //   A: pull=down
  //   aluResult: pull=down
  //   flags_GT: pull=down
  //   flags_E: pull=down
  //   B: pull=down
  //   Operand 1
  //   Operand 2
  //   Provide operands to their respective functions.
  //   Compare instruction needs registers as we need to keep the value of the flags stored.
endmodule

module EXU (
  input  isBeq,
  input  isUbranch,
  input  isBgt,
  input  isRet,
  input  [31:0] branchTargetIn,
  input  [31:0] A,
  input  [3:0] aluSignals,
  input  [31:0] B,
  input  Clock,
  output isBranchTaken,
  output [23:0] branchTargetOut,
  output [31:0] ALUResult
);

  wire and_1_out, and_2_out, flags_E, flags_GT;
  wire [31:24] multiplexer_1_out;

  and and_1 (and_1_out, isBeq, flags_E);
  and and_2 (and_2_out, isBgt, flags_GT);
  ALU alu_1 (
    .A(A), .aluSignals(aluSignals), .B(B), .clock(Clock), .aluResult(ALUResult), .flags_GT(flags_GT),
    .flags_E(flags_E));
  Multiplexer #(.width(32), .enable("false")) multiplexer_1 (
    .in0(branchTargetIn), .in1(A), .out({multiplexer_1_out, branchTargetOut}), .sel(isRet));
  or or_1 (isBranchTaken, and_1_out, isUbranch, and_2_out);

  // Notes on the sheet:
  //   branchTargetOut: pull=down
  //   isBgt: pull=down
  //   isUbranch: pull=down
  //   isBeq: pull=down
  //   ALUResult: pull=down
  //   branchTargetIn: pull=down
  //   isBranchTaken: pull=down
  //   B: pull=down
  //   A: pull=down
  //   aluSignals: pull=down
  //   (Operand 1)
  //   (Operand 2)
  //   EX Stage
  //   (To be sent to the IF Stage)
endmodule

// IF-OF Latch
module IF_OF (
  input  [31:0] INSIN,
  input  CLKIN,
  input  [23:0] PCIN,
  output [31:0] InsOut,
  output [23:0] PcOut
);

  Register #(.width(32), .trigger("falling")) register_1 (.D(INSIN), .Q(InsOut), .clk(CLKIN));  // open: en, clr
  Register #(.width(24), .trigger("falling")) register_2 (.D(PCIN), .Q(PcOut), .clk(CLKIN));  // open: en, clr
endmodule

module OF_EX (
  input  [31:0] InsIN,
  input  [23:0] PcIn,
  input  [12:0] ControlIn,
  input  [31:0] BranchTargetIn,
  input  CLKOFEX,
  input  [31:0] AIn,
  input  [31:0] BIn,
  input  [31:0] OP2In,
  output [31:0] InsOut,
  output [23:0] PcOut,
  output [12:0] ControlOut,
  output [31:0] BranchTargetOut,
  output [31:0] AOut,
  output [31:0] BOut,
  output [31:0] OP2Out
);

  Register #(.width(32), .trigger("falling")) register_1 (.D(InsIN), .Q(InsOut), .clk(CLKOFEX));  // open: en, clr
  Register #(.width(24), .trigger("falling")) register_2 (.D(PcIn), .Q(PcOut), .clk(CLKOFEX));  // open: en, clr
  Register #(.width(13), .trigger("falling")) register_3 (
    .D(ControlIn), .Q(ControlOut), .clk(CLKOFEX));  // open: en, clr
  Register #(.width(32), .trigger("falling")) register_4 (
    .D(BranchTargetIn), .Q(BranchTargetOut), .clk(CLKOFEX));  // open: en, clr
  Register #(.width(32), .trigger("falling")) register_5 (.D(AIn), .Q(AOut), .clk(CLKOFEX));  // open: en, clr
  Register #(.width(32), .trigger("falling")) register_6 (.D(BIn), .Q(BOut), .clk(CLKOFEX));  // open: en, clr
  Register #(.width(32), .trigger("falling")) register_7 (.D(OP2In), .Q(OP2Out), .clk(CLKOFEX));  // open: en, clr
endmodule

// EX-MA Latch
module EX_MA (
  input  [23:0] PcIn,
  input  [31:0] AluIn,
  input  [31:0] InsIn,
  input  ClkIN,
  input  [31:0] op2In,
  input  [12:0] ControlIn,
  output [23:0] PcOut,
  output [31:0] AluOut,
  output [31:0] InsOut,
  output [31:0] Op2Out,
  output [12:0] ControlOut
);

  Register #(.width(24), .trigger("falling")) register_1 (.D(PcIn), .Q(PcOut), .clk(ClkIN));  // open: en, clr
  Register #(.width(32), .trigger("falling")) register_2 (.D(AluIn), .Q(AluOut), .clk(ClkIN));  // open: en, clr
  Register #(.width(32), .trigger("falling")) register_3 (.D(InsIn), .Q(InsOut), .clk(ClkIN));  // open: en, clr
  Register #(.width(32), .trigger("falling")) register_4 (.D(op2In), .Q(Op2Out), .clk(ClkIN));  // open: en, clr
  Register #(.width(13), .trigger("falling")) register_5 (.D(ControlIn), .Q(ControlOut), .clk(ClkIN));  // open: en, clr
endmodule

// MA-RW Latch
module MA_RW (
  input  [23:0] PCIn,
  input  [31:0] LdIn,
  input  [31:0] AluIn,
  input  CLK,
  input  [31:0] InsIn,
  input  [12:0] CtrlIn,
  output [23:0] PCOut,
  output [31:0] LdOut,
  output [31:0] AluOut,
  output [31:0] InsOut,
  output [12:0] CtrlOut
);

  Register #(.width(24), .trigger("falling")) register_1 (.D(PCIn), .Q(PCOut), .clk(CLK));  // open: en, clr
  Register #(.width(32), .trigger("falling")) register_2 (.D(LdIn), .Q(LdOut), .clk(CLK));  // open: en, clr
  Register #(.width(32), .trigger("falling")) register_3 (.D(AluIn), .Q(AluOut), .clk(CLK));  // open: en, clr
  Register #(.width(32), .trigger("falling")) register_4 (.D(InsIn), .Q(InsOut), .clk(CLK));  // open: en, clr
  Register #(.width(13), .trigger("falling")) register_5 (.D(CtrlIn), .Q(CtrlOut), .clk(CLK));  // open: en, clr
endmodule

module Split_Control_OFEX (
  input  [12:0] Control_In,
  output isUBranch_out,
  output [3:0] ALU_Signal_out,
  output isBeqout,
  output isRetout,
  output IsBgtout
);


  assign ALU_Signal_out = Control_In[6:3];
  assign isBeqout = Control_In[8];
  assign IsBgtout = Control_In[11];
  assign isRetout = Control_In[9];
  assign isUBranch_out = Control_In[1];
endmodule

module Split_Control_EXMA (
  input  [12:0] Control_IN,
  output is_Ret_out,
  output is_St_out
);


  assign is_Ret_out = Control_IN[7];
  assign is_St_out = Control_IN[12];
endmodule

module Split_Control_MARW (
  input  [12:0] Control_In,
  output isWb_out,
  output isLoad_out,
  output isCall_out
);


  assign isCall_out = Control_In[10];
  assign isLoad_out = Control_In[7];
  assign isWb_out = Control_In[0];
endmodule

module Split_Control (
  input  [12:0] Control_In,
  output isWb_out,
  output isUbranch_out,
  output isImm_out,
  output [3:0] ALU_signals,
  output isLoad_out,
  output isBeq_out,
  output isRet_out,
  output isCall_out,
  output isBgt_out,
  output isStore_out
);


  assign ALU_signals = Control_In[6:3];
  assign isBeq_out = Control_In[8];
  assign isBgt_out = Control_In[11];
  assign isCall_out = Control_In[10];
  assign isImm_out = Control_In[2];
  assign isLoad_out = Control_In[7];
  assign isRet_out = Control_In[9];
  assign isStore_out = Control_In[12];
  assign isUbranch_out = Control_In[1];
  assign isWb_out = Control_In[0];
endmodule

// Algo6 RWEX
module Algo6 (
  input  [31:0] A,
  input  [31:0] B,
  output Algo6Out
);

  wire comparator_1_eq, comparator_2_eq, comparator_3_eq, comparator_4_eq, cu_1_isbeq, cu_1_isbgt,
       cu_1_iscall, cu_1_isret, cu_1_isubranch, cu_2_isbeq, cu_2_isbgt, cu_2_iscall, cu_2_isret, cu_2_isst,
       cu_2_isubranch, not_1_out, or_1_out, or_2_out, or_3_out;
  wire [3:0] multiplexer_1_out, multiplexer_2_out;

  Comparator #(.width(5)) comparator_1 (.a(B[31:27]), .b(5'b00101), .eq(comparator_1_eq));  // open: gt, lt
  CU cu_1 (
    .isUbranch(cu_1_isubranch), .isBeq(cu_1_isbeq), .isBgt(cu_1_isbgt), .isCall(cu_1_iscall),
    .isRet(cu_1_isret), .Instruction(A));  // open: isWb, isImmediate, isLd, isSt, ALUSignals
  CU cu_2 (
    .isUbranch(cu_2_isubranch), .isSt(cu_2_isst), .isBeq(cu_2_isbeq), .isBgt(cu_2_isbgt),
    .isCall(cu_2_iscall), .isRet(cu_2_isret), .Instruction(B));  // open: isWb, isImmediate, isLd, ALUSignals
  Comparator #(.width(5)) comparator_2 (.a(B[31:27]), .b(5'b01101), .eq(comparator_2_eq));  // open: gt, lt
  Comparator #(.width(5)) comparator_3 (.a(A[31:27]), .b(5'b01101), .eq(comparator_3_eq));  // open: gt, lt
  or or_1 (or_1_out, cu_1_isubranch, cu_1_isbeq, comparator_3_eq, cu_1_iscall, cu_1_isbgt);
  or or_2 (or_2_out, cu_2_isubranch, comparator_1_eq, comparator_2_eq, cu_2_isbeq, cu_2_isret, cu_2_isbgt, cu_2_isst);
  or or_3 (or_3_out, or_1_out, or_2_out);
  not not_1 (not_1_out, or_3_out);
  Multiplexer #(.width(4), .enable("false")) multiplexer_1 (
    .in0(A[21:18]), .in1(4'b1111), .out(multiplexer_1_out), .sel(cu_1_isret));
  Multiplexer #(.width(4), .enable("false")) multiplexer_2 (
    .in0(B[25:22]), .in1(4'b1111), .out(multiplexer_2_out), .sel(cu_2_iscall));
  and and_1 (Algo6Out, not_1_out, comparator_4_eq);
  Comparator #(.width(4)) comparator_4 (
    .a(multiplexer_1_out), .b(multiplexer_2_out), .eq(comparator_4_eq));  // open: gt, lt

  // Notes on the sheet:
  //   rd
  //   rs1
  //   opcode
  //   rs2
  //   rs1
  //   rd
  //   opcode 
  //   opcode
endmodule

// Algo7 RWMA
module Algo7 (
  input  [31:0] A,
  input  [31:0] B,
  output Algo7Out
);

  wire and_1_out, and_2_out, comparator_1_eq, comparator_2_eq, comparator_3_eq, comparator_4_eq, cu_1_isbeq,
       cu_1_isbgt, cu_1_iscall, cu_1_isimmediate, cu_1_isst, cu_1_isubranch, cu_2_isbeq, cu_2_isbgt,
       cu_2_iscall, cu_2_isret, cu_2_isst, cu_2_isubranch, not_1_out, not_2_out, not_3_out, not_4_out,
       or_1_out, or_2_out;
  wire [3:0] cu_2_alusignals, DEST, SRC2;

  Comparator #(.width(5)) comparator_1 (.a(B[31:27]), .b(5'b01101), .eq(comparator_1_eq));  // open: gt, lt
  Comparator #(.width(5)) comparator_2 (.a(A[31:27]), .b(5'b01101), .eq(comparator_2_eq));  // open: gt, lt
  CU cu_1 (
    .isUbranch(cu_1_isubranch), .isImmediate(cu_1_isimmediate), .isSt(cu_1_isst), .isBeq(cu_1_isbeq),
    .isBgt(cu_1_isbgt), .isCall(cu_1_iscall), .Instruction(A));  // open: isWb, isLd, isRet, ALUSignals
  CU cu_2 (
    .isUbranch(cu_2_isubranch), .isSt(cu_2_isst), .isBeq(cu_2_isbeq), .isBgt(cu_2_isbgt),
    .isCall(cu_2_iscall), .isRet(cu_2_isret), .ALUSignals(cu_2_alusignals), .Instruction(B));  // open: isWb, isImmediate, isLd
  Comparator #(.width(5)) comparator_3 (.a(B[31:27]), .b(5'b00101), .eq(comparator_3_eq));  // open: gt, lt
  or or_1 (or_1_out, cu_1_isubranch, cu_1_isbeq, comparator_2_eq, cu_1_iscall, cu_1_isbgt);
  not not_1 (not_1_out, cu_1_isst);
  Multiplexer #(.width(4), .enable("false")) multiplexer_1 (
    .in0(B[25:22]), .in1(4'b1111), .out(DEST), .sel(cu_2_iscall));
  or or_2 (or_2_out, cu_2_isubranch, comparator_3_eq, cu_2_isbeq, cu_2_isret, comparator_1_eq, cu_2_isbgt, cu_2_isst);
  and and_1 (and_1_out, cu_1_isimmediate, not_1_out);
  Multiplexer #(.width(4), .enable("false")) multiplexer_2 (
    .in0(A[17:14]), .in1(A[25:22]), .out(SRC2), .sel(cu_1_isst));
  Comparator #(.width(4)) comparator_4 (.a(SRC2), .b(DEST), .eq(comparator_4_eq));  // open: gt, lt
  not not_2 (not_2_out, or_1_out);
  not not_3 (not_3_out, and_1_out);
  not not_4 (not_4_out, or_2_out);
  and and_2 (and_2_out, not_2_out, not_3_out, not_4_out);
  and and_3 (Algo7Out, and_2_out, comparator_4_eq);

  // Notes on the sheet:
  //   rd
  //   rs1
  //   opcode
  //   rs2
  //   rd
  //   opcode
  //   rs2
  //   rs1
endmodule

module Algo5 (
  input  [31:0] A,
  input  [31:0] B,
  output outbit
);

  wire and_1_out, and_2_out, comparator_1_eq, comparator_2_eq, comparator_3_eq, cu_1_isbeq, cu_1_isbgt,
       cu_1_iscall, cu_1_isimmediate, cu_1_isret, cu_1_isst, cu_1_isubranch, cu_2_iscall, cu_2_isld,
       not_1_out, not_2_out, not_3_out, not_4_out, or_1_out, or_2_out, or_3_out;
  wire [3:0] multiplexer_1_out, multiplexer_2_out, multiplexer_3_out;

  CU cu_1 (
    .isUbranch(cu_1_isubranch), .isImmediate(cu_1_isimmediate), .isSt(cu_1_isst), .isBeq(cu_1_isbeq),
    .isBgt(cu_1_isbgt), .isCall(cu_1_iscall), .isRet(cu_1_isret), .Instruction(A));  // open: isWb, isLd, ALUSignals
  CU cu_2 (
    .isLd(cu_2_isld), .isCall(cu_2_iscall), .Instruction(B));  // open: isWb, isUbranch, isImmediate, isSt, isBeq, isBgt, isRet, ALUSignals
  Comparator #(.width(5)) comparator_1 (.a(A[31:27]), .b(5'b01101), .eq(comparator_1_eq));  // open: gt, lt
  not not_1 (not_1_out, cu_2_isld);
  or or_1 (or_1_out, cu_1_isubranch, cu_1_isbeq, comparator_1_eq, cu_1_iscall, cu_1_isbgt);
  Multiplexer #(.width(4), .enable("false")) multiplexer_1 (
    .in0(B[25:22]), .in1(4'b1111), .out(multiplexer_1_out), .sel(cu_2_iscall));
  or or_2 (or_2_out, or_1_out, not_1_out);
  not not_2 (not_2_out, or_2_out);
  not not_3 (not_3_out, cu_1_isst);
  Multiplexer #(.width(4), .enable("false")) multiplexer_2 (
    .in0(A[17:14]), .in1(A[25:22]), .out(multiplexer_2_out), .sel(cu_1_isst));
  and and_1 (and_1_out, cu_1_isimmediate, not_3_out);
  Multiplexer #(.width(4), .enable("false")) multiplexer_3 (
    .in0(A[21:18]), .in1(4'b1111), .out(multiplexer_3_out), .sel(cu_1_isret));
  Comparator #(.width(4)) comparator_2 (
    .a(multiplexer_2_out), .b(multiplexer_1_out), .eq(comparator_2_eq));  // open: gt, lt
  not not_4 (not_4_out, and_1_out);
  and and_2 (and_2_out, not_4_out, comparator_2_eq);
  Comparator #(.width(4)) comparator_3 (
    .a(multiplexer_3_out), .b(multiplexer_1_out), .eq(comparator_3_eq));  // open: gt, lt
  or or_3 (or_3_out, and_2_out, comparator_3_eq);
  and and_3 (outbit, not_2_out, or_3_out);

  // Notes on the sheet:
  //   rd
  //   opcode
  //   rs2
  //   rs1
  //   rd
  //   rs2
  //   rs1
  //   opcode
  //   dest
  //   src2
  //   src1
  //   hassrc2
endmodule
